# Fritzing sketch design_schematic (saved by Fritzing 0.9.10b)

parts:
  Part1 = Arduino Uno (Rev3) - ICSP
  VCC2 = Battery  # not connected
  Part4 = Bluetooth HC-05 Macho
  M2 = DC Motor [voltage_(max)=6V voltage_(min)=3V]  # not connected
  M3 = DC Motor [voltage_(max)=6V voltage_(min)=3V]  # not connected
  M4 = DC Motor [voltage_(max)=6V voltage_(min)=3V]  # not connected
  M5 = DC Motor [voltage_(max)=6V voltage_(min)=3V]  # not connected
  Part5 = Arduino Sensor Shield v5.0  # not connected
  J1 = Basic Servo  # not connected
  HC-SR04_Sensor_1 = HC-SR04 Ultrasonic Distance Sensor  # not connected
  Part6 = PowerBoost 500 Charger  # not connected

nets:
  5V: Part1.5V, Part4.VCC
  GND: Part1.GND, Part4.GND

notes:
  Power Source
  Bluetooth Module
  Battery Charger
  Expansion board
